// Digital circuit 2.dig as structural Verilog
module _2 (
  input  Sel1,
  input  Sel2,
  input  D,
  output S0,
  output S1,
  output S2,
  output S3
);

  wire not_1_out, not_2_out;

  not not_1 (not_1_out, Sel1);
  not not_2 (not_2_out, Sel2);
  and and_1 (S3, D, Sel1, Sel2);
  and and_2 (S2, D, Sel1, not_2_out);
  and and_3 (S1, D, not_1_out, Sel2);
  and and_4 (S0, D, not_1_out, not_2_out);

  // Notes on the sheet:
  //   El demultiplexor funciona como el espejo del multiplexor por lo que se utiliza el mismo concepto del mux solo 
  //   que a diferencia de tener una salida común se tiene una entrada común. Como se tienen 4 salidas no se coloca 
  //   la compuerta OR.
endmodule
