// Digital circuit 3a.dig as structural Verilog
module _3a (
  input  S,
  input  R,
  input  S_2,
  input  R_2,
  input  Clock,
  input  C,
  output Q,
  output Q_2,
  output Q_3
);

  wire nand_1_out, nand_2_out, nand_3_out, nand_4_out, nand_5_out, nand_6_out, not_1_out;

  RS_FF rs_ff_1 (.S(S_2), .C(C), .R(R_2), .Q(Q));  // open: nQ
  nand nand_1 (nand_1_out, S, Clock);
  nand nand_2 (nand_2_out, Clock, R);
  nand nand_3 (nand_3_out, nand_1_out, nand_4_out);
  nand nand_4 (nand_4_out, nand_3_out, nand_2_out);
  not not_1 (not_1_out, Clock);
  nand nand_5 (nand_5_out, nand_3_out, not_1_out);
  nand nand_6 (nand_6_out, not_1_out, nand_4_out);
  nand nand_7 (Q_2, nand_5_out, Q_3);
  nand nand_8 (Q_3, Q_2, nand_6_out);

  // Notes on the sheet:
  //   Clock: Hz: 5
  //   C: Hz: 5
  //   FlipFlop RS
  //   El circuito responde cuando el clock está activado, es decir, cuando hace la transición de pendiente 
  //   positiva. Esto permite cambiar el valor de Q según las entradas S y R. S sirve para establecer el valor (1)
  //    y R sirve para restablecer el valor (0). Cuando S y R se activan a la vez, Q y Q' tienen el mismo valor y al 
  //   cambiar el estado el sistema oscila, es decir, la respuesta es indeterminada ya que no se tiene certeza de 
  //   cuál señal cambia primero.
endmodule
