// Digital circuit 3b.dig as structural Verilog
module _3b (
  input  J,
  input  K,
  input  J_2,
  input  K_2,
  input  Clock,
  input  Clock_2,
  output Q,
  output Q_2,
  output Q_3
);

  wire nand_1_out, nand_2_out, nand_3_out, nand_4_out, nand_5_out, nand_6_out, not_1_out;

  JK_FF jk_ff_1 (.J(J), .C(Clock_2), .K(K), .Q(Q));  // open: nQ
  nand nand_1 (nand_1_out, Q_3, J_2, Clock);
  nand nand_2 (nand_2_out, Clock, K_2, Q_2);
  nand nand_3 (nand_3_out, nand_1_out, nand_4_out);
  nand nand_4 (nand_4_out, nand_3_out, nand_2_out);
  not not_1 (not_1_out, Clock);
  nand nand_5 (nand_5_out, nand_3_out, not_1_out);
  nand nand_6 (nand_6_out, not_1_out, nand_4_out);
  nand nand_7 (Q_2, nand_5_out, Q_3);
  nand nand_8 (Q_3, Q_2, nand_6_out);

  // Notes on the sheet:
  //   Clock_2: Hz: 5
  //   El FlipFlop se dipara por el flanco de pendiente positiva del reloj. Funciona similarmente que 
  //   el flipflop RS sólo que en este caso si J y K son 1 no hay una salida indeterminada, es decir, Q
  //   cambiará su valor cada vez que cambie la señal del reloj. Esto ocurre porque el estado de Q 
  //   condiciona la entrada del primer latch y a su vez la del segundo latch haciendo que Q y Q' 
  //   simpre tengan valores diferentes.
  //   FlipFlop JK
endmodule
