// Digital circuit 4.dig as structural Verilog
module _4 (
  input  Set,
  input  Enable,
  input  Clear,
  input  D3,
  input  D2,
  input  D1,
  input  D0,
  input  Set_2,
  input  Enable_2,
  input  Clear_2,
  input  Set_3,
  input  Enable_3,
  input  Clear_3,
  input  In3,
  input  In2,
  input  In1,
  input  In0,
  input  Clock,
  input  Clock_2,
  input  I0,
  input  I1,
  input  I2,
  input  I3,
  input  Clock_3,
  output out_1,
  output out_2,
  output out_3,
  output out_4,
  output O3,
  output O2,
  output O1,
  output O0
);

  wire A0, A1, A2, A3, d_ff_as_5_q, d_ff_as_6_q, d_ff_as_7_q, d_ff_as_9_q, multiplexer_1_out,
       multiplexer_2_out, multiplexer_3_out, multiplexer_4_out, multiplexer_5_out, multiplexer_6_out,
       multiplexer_7_out, multiplexer_8_out, multiplexer_9_out, multiplexer_10_out, multiplexer_11_out,
       multiplexer_12_out, S0, S1, S2, S3;

  Multiplexer multiplexer_1 (.sel(Enable_2), .in_0(S3), .in_1(D3), .out(multiplexer_1_out));
  D_FF_AS d_ff_as_1 (.Set(Set_2), .D(multiplexer_1_out), .C(Clock), .Clr(Clear_2), .Q(S3));  // open: nQ
  Multiplexer multiplexer_2 (.sel(Enable_2), .in_0(S2), .in_1(D2), .out(multiplexer_2_out));
  D_FF_AS d_ff_as_2 (.Set(Set_2), .D(multiplexer_2_out), .C(Clock), .Clr(Clear_2), .Q(S2));  // open: nQ
  Multiplexer multiplexer_3 (.sel(Enable_2), .in_0(S1), .in_1(D1), .out(multiplexer_3_out));
  D_FF_AS d_ff_as_3 (.Set(Set_2), .D(multiplexer_3_out), .C(Clock), .Clr(Clear_2), .Q(S1));  // open: nQ
  Multiplexer multiplexer_4 (.sel(Enable_2), .in_0(S0), .in_1(D0), .out(multiplexer_4_out));
  Multiplexer multiplexer_5 (.sel(Enable_3), .in_0(d_ff_as_5_q), .in_1(In3), .out(multiplexer_5_out));
  D_FF_AS d_ff_as_4 (.Set(Set_2), .D(multiplexer_4_out), .C(Clock), .Clr(Clear_2), .Q(S0));  // open: nQ
  D_FF_AS d_ff_as_5 (.Set(Set_3), .D(multiplexer_5_out), .C(Clock_2), .Clr(Clear_3), .Q(d_ff_as_5_q));  // open: nQ
  assign O3 = ~d_ff_as_5_q ? S3 : 1'bz;  // DriverInvSel driverinvsel_1
  assign A3 = d_ff_as_5_q ? I3 : 1'bz;  // Driver driver_1
  Multiplexer multiplexer_6 (.sel(Enable_3), .in_0(d_ff_as_6_q), .in_1(In2), .out(multiplexer_6_out));
  D_FF_AS d_ff_as_6 (.Set(Set_3), .D(multiplexer_6_out), .C(Clock_2), .Clr(Clear_3), .Q(d_ff_as_6_q));  // open: nQ
  assign O2 = ~d_ff_as_6_q ? S2 : 1'bz;  // DriverInvSel driverinvsel_2
  assign A2 = d_ff_as_6_q ? I2 : 1'bz;  // Driver driver_2
  PullDown pulldown_1 (.out(A3));
  Multiplexer multiplexer_7 (.sel(Enable_3), .in_0(d_ff_as_7_q), .in_1(In1), .out(multiplexer_7_out));
  Multiplexer multiplexer_8 (.sel(Enable), .in_0(out_1), .in_1(A3), .out(multiplexer_8_out));
  D_FF_AS d_ff_as_7 (.Set(Set_3), .D(multiplexer_7_out), .C(Clock_2), .Clr(Clear_3), .Q(d_ff_as_7_q));  // open: nQ
  D_FF_AS d_ff_as_8 (.Set(Set), .D(multiplexer_8_out), .C(Clock_3), .Clr(Clear), .Q(out_1));  // open: nQ
  assign O1 = ~d_ff_as_7_q ? S1 : 1'bz;  // DriverInvSel driverinvsel_3
  assign A1 = d_ff_as_7_q ? I1 : 1'bz;  // Driver driver_3
  PullDown pulldown_2 (.out(A2));
  Multiplexer multiplexer_9 (.sel(Enable_3), .in_0(d_ff_as_9_q), .in_1(In0), .out(multiplexer_9_out));
  Multiplexer multiplexer_10 (.sel(Enable), .in_0(out_2), .in_1(A2), .out(multiplexer_10_out));
  D_FF_AS d_ff_as_9 (.Set(Set_3), .D(multiplexer_9_out), .C(Clock_2), .Clr(Clear_3), .Q(d_ff_as_9_q));  // open: nQ
  D_FF_AS d_ff_as_10 (.Set(Set), .D(multiplexer_10_out), .C(Clock_3), .Clr(Clear), .Q(out_2));  // open: nQ
  assign O0 = ~d_ff_as_9_q ? S0 : 1'bz;  // DriverInvSel driverinvsel_4
  PullDown pulldown_3 (.out(A1));
  assign A0 = d_ff_as_9_q ? I0 : 1'bz;  // Driver driver_4
  Multiplexer multiplexer_11 (.sel(Enable), .in_0(out_3), .in_1(A1), .out(multiplexer_11_out));
  D_FF_AS d_ff_as_11 (.Set(Set), .D(multiplexer_11_out), .C(Clock_3), .Clr(Clear), .Q(out_3));  // open: nQ
  PullDown pulldown_4 (.out(A0));
  Multiplexer multiplexer_12 (.sel(Enable), .in_0(out_4), .in_1(A0), .out(multiplexer_12_out));
  D_FF_AS d_ff_as_12 (.Set(Set), .D(multiplexer_12_out), .C(Clock_3), .Clr(Clear), .Q(out_4));  // open: nQ

  // Notes on the sheet:
  //   Clock: Hz: 5
  //   Clock_2: Hz: 5
  //   Clock_3: Hz: 5
  //   Registro de control de salidas
  //   Registro de configuración
  //   Registro de almacenamiento del estado del pin
endmodule
